# Fritzing sketch ButtonClickCheck (saved by Fritzing 0.9.3b)
breadboards: 1

parts:
  부품3 = Arduino Uno (Rev3)
  S3 = Pushbutton [package="[THT]"]
  R3 = Resistor [tolerance=±5% resistance=10k package=THT]
  R4 = Resistor [tolerance=±5% resistance=10k package=THT]
  S4 = Pushbutton [package="[THT]"]

nets:
  N1: 부품3.D2, S3.Pin_1, S3.Pin_2, R3.Pin_0
  N2: 부품3.D4, 부품3.GND, R3.Pin_1, R4.Pin_1, S4.Pin_3, S4.Pin_4
  N3: 부품3.5V, S3.Pin_3, S3.Pin_4, R4.Pin_0
  N4: S4.Pin_1, S4.Pin_2
